# Fritzing sketch rgb (saved by Fritzing 0.9.3b)
breadboards: 1

parts:
  Arduino_Uno = Arduino Uno (Rev3)
  Piezo_Buzzer = Piezo Speaker [part_number=PKM17EPP-4001-B0]
  R1 = Resistor [tolerance=±5% resistance=100 package=THT]
  R2 = Resistor [tolerance=±5% resistance=220 package=THT]
  R3 = Resistor [tolerance=±5% resistance=220 package=THT]
  R4 = Resistor [tolerance=±5% resistance=220 package=THT]
  R5 = Resistor [tolerance=±5% resistance=220 package=THT]
  R6 = Resistor [tolerance=±5% resistance=220 package=THT]
  R7 = Resistor [tolerance=±5% resistance=220 package=THT]
  R8 = Resistor [tolerance=±5% resistance=220 package=THT]
  R9 = Resistor [tolerance=±5% resistance=220 package=THT]
  R10 = Resistor [tolerance=±5% resistance=220 package=THT]
  R11 = Resistor [tolerance=±5% resistance=220 package=THT]
  R12 = Resistor [tolerance=±5% resistance=220 package=THT]
  S1 = Pushbutton [package="[THT]"]
  R13 = Resistor [tolerance=±5% resistance=220 package=THT]
  LED1 = RGB LED - (4 legs) [package="5 mm [THT]"]

nets:
  N1: Arduino_Uno.A0, S1.Pin_1, S1.Pin_2, R13.Pin_1
  N2: Arduino_Uno.A2, LED1.red_cathode
  N3: Arduino_Uno.A3, LED1.common_anode
  N4: Arduino_Uno.A4/SDA, LED1.blue_cathode
  N5: Arduino_Uno.D8, R8.Pin_1
  N6: Arduino_Uno.D9_PWM, R9.Pin_1
  N7: Arduino_Uno.D10_PWM/SS, R10.Pin_1
  N8: Arduino_Uno.D11_PWM/MOSI, R11.Pin_1
  N9: Arduino_Uno.D12/MISO, R12.Pin_1
  N10: Arduino_Uno.D13/SCK, R1.Pin_1
  N11: Arduino_Uno.D2, Arduino_Uno.5V, R2.Pin_1, S1.Pin_3, S1.Pin_4
  N12: Arduino_Uno.D3_PWM, R3.Pin_1
  N13: Arduino_Uno.D4, R4.Pin_1
  N14: Arduino_Uno.D5_PWM, R5.Pin_1
  N15: Arduino_Uno.D6_PWM, R6.Pin_1
  N16: Arduino_Uno.D7, R7.Pin_1
  N17: Arduino_Uno.GND, Piezo_Buzzer.pin1, R2.Pin_0, R3.Pin_0, R4.Pin_0, R5.Pin_0, R6.Pin_0, R7.Pin_0, R8.Pin_0, R9.Pin_0, R10.Pin_0, R11.Pin_0, R12.Pin_0, R13.Pin_0, LED1.green_cathode
  N18: Piezo_Buzzer.pin2, R1.Pin_0
